// Logisim project conway.circ as structural Verilog: 17 circuits, main circuit grid_calc_row_by_row
module popcount (
  input  A,
  input  B,
  input  C,
  input  D,
  input  E,
  input  F,
  input  G,
  input  H,
  output [3:0] CNT
);

  wire [3:0] adder_1_out, adder_2_out, adder_3_out, adder_4_out, adder_5_out, adder_6_out,
       bit_extender_1_out, bit_extender_2_out, bit_extender_3_out, bit_extender_4_out, bit_extender_5_out,
       bit_extender_6_out, bit_extender_7_out, bit_extender_8_out;

  assign bit_extender_1_out = {{3{1'b0}}, A};  // Bit_Extender bit_extender_1
  assign bit_extender_2_out = {{3{1'b0}}, B};  // Bit_Extender bit_extender_2
  assign bit_extender_3_out = {{3{1'b0}}, C};  // Bit_Extender bit_extender_3
  assign bit_extender_4_out = {{3{1'b0}}, D};  // Bit_Extender bit_extender_4
  assign bit_extender_5_out = {{3{1'b0}}, E};  // Bit_Extender bit_extender_5
  assign bit_extender_6_out = {{3{1'b0}}, F};  // Bit_Extender bit_extender_6
  assign bit_extender_7_out = {{3{1'b0}}, G};  // Bit_Extender bit_extender_7
  assign bit_extender_8_out = {{3{1'b0}}, H};  // Bit_Extender bit_extender_8
  Adder #(.width(4)) adder_1 (.a(bit_extender_1_out), .b(bit_extender_2_out), .out(adder_1_out));  // open: cin, cout
  Adder #(.width(4)) adder_2 (.a(bit_extender_3_out), .b(bit_extender_4_out), .out(adder_2_out));  // open: cin, cout
  Adder #(.width(4)) adder_3 (.a(bit_extender_5_out), .b(bit_extender_6_out), .out(adder_3_out));  // open: cin, cout
  Adder #(.width(4)) adder_4 (.a(bit_extender_7_out), .b(bit_extender_8_out), .out(adder_4_out));  // open: cin, cout
  Adder #(.width(4)) adder_5 (.a(adder_1_out), .b(adder_2_out), .out(adder_5_out));  // open: cin, cout
  Adder #(.width(4)) adder_6 (.a(adder_3_out), .b(adder_4_out), .out(adder_6_out));  // open: cin, cout
  Adder #(.width(4)) adder_7 (.a(adder_5_out), .b(adder_6_out), .out(CNT));  // open: cin, cout
endmodule

module single_cell (
  input  ME,
  input  NE,
  input  N,
  input  NW,
  input  W,
  input  E,
  input  SW,
  input  S,
  input  SE,
  output ME_N,
  output ME_S,
  output ME_E,
  output ME_W,
  output ALIVE
);

  wire and_1_out, and_2_out, comparator_1_eq, comparator_2_eq, or_1_out;
  wire [3:0] counter_cnt;

  popcount counter (.A(NE), .B(N), .C(NW), .D(W), .E(E), .F(SW), .G(S), .H(SE), .CNT(counter_cnt));
  Comparator #(.mode("unsigned"), .width(4)) comparator_1 (
    .a(counter_cnt), .b(4'b0010), .eq(comparator_1_eq));  // open: gt, lt
  Comparator #(.mode("unsigned"), .width(4)) comparator_2 (
    .a(counter_cnt), .b(4'b0011), .eq(comparator_2_eq));  // open: gt, lt
  or or_1 (or_1_out, comparator_1_eq, comparator_2_eq);
  and and_1 (and_1_out, ME, or_1_out);
  and and_2 (and_2_out, ~ME, comparator_2_eq);  // AND_Gate
  or or_2 (ALIVE, and_1_out, and_2_out);

  assign ME_E = ME;
  assign ME_N = ME;
  assign ME_S = ME;
  assign ME_W = ME;

  // Notes on the sheet:
  //   Rule 2: If alive and 2 or 3 Neighbors lives
  //   Rule 4: If dead and 3 neighbors, lives (reproduction)
  //   Rule 1: If alive and less than 2 Neighbors dies (Underpopulation)
  //   Rule 3: If alive and more than 3 neighbors dies (overpopulation)
  //   We only need to output value based on if we are alive or not. So we can exclude rules 1 and 3 from calculation
  //   Rule 2
  //   Rule 4
endmodule

module main (
  input  LOAD_RUN,
  input  CLK_EN,
  input  RESET
);

  wire and_1_out, CLK_out;
  wire [7:0] IN_ROW_1_sw8, IN_ROW_2_sw8, IN_ROW_3_sw8, IN_ROW_4_sw8, IN_ROW_5_sw8, IN_ROW_6_sw8,
       IN_ROW_7_sw8, IN_ROW_8_sw8;
  wire [63:0] cell_grid_1_grid_out, system_memory_1_mem_out;

  DipSwitch IN_ROW_1 (
    .sw1(IN_ROW_1_sw8[7]), .sw2(IN_ROW_1_sw8[6]), .sw3(IN_ROW_1_sw8[5]), .sw4(IN_ROW_1_sw8[4]),
    .sw5(IN_ROW_1_sw8[3]), .sw6(IN_ROW_1_sw8[2]), .sw7(IN_ROW_1_sw8[1]), .sw8(IN_ROW_1_sw8[0]));
  DipSwitch IN_ROW_2 (
    .sw1(IN_ROW_2_sw8[7]), .sw2(IN_ROW_2_sw8[6]), .sw3(IN_ROW_2_sw8[5]), .sw4(IN_ROW_2_sw8[4]),
    .sw5(IN_ROW_2_sw8[3]), .sw6(IN_ROW_2_sw8[2]), .sw7(IN_ROW_2_sw8[1]), .sw8(IN_ROW_2_sw8[0]));
  DipSwitch IN_ROW_3 (
    .sw1(IN_ROW_3_sw8[7]), .sw2(IN_ROW_3_sw8[6]), .sw3(IN_ROW_3_sw8[5]), .sw4(IN_ROW_3_sw8[4]),
    .sw5(IN_ROW_3_sw8[3]), .sw6(IN_ROW_3_sw8[2]), .sw7(IN_ROW_3_sw8[1]), .sw8(IN_ROW_3_sw8[0]));
  DipSwitch IN_ROW_4 (
    .sw1(IN_ROW_4_sw8[7]), .sw2(IN_ROW_4_sw8[6]), .sw3(IN_ROW_4_sw8[5]), .sw4(IN_ROW_4_sw8[4]),
    .sw5(IN_ROW_4_sw8[3]), .sw6(IN_ROW_4_sw8[2]), .sw7(IN_ROW_4_sw8[1]), .sw8(IN_ROW_4_sw8[0]));
  DipSwitch IN_ROW_5 (
    .sw1(IN_ROW_5_sw8[7]), .sw2(IN_ROW_5_sw8[6]), .sw3(IN_ROW_5_sw8[5]), .sw4(IN_ROW_5_sw8[4]),
    .sw5(IN_ROW_5_sw8[3]), .sw6(IN_ROW_5_sw8[2]), .sw7(IN_ROW_5_sw8[1]), .sw8(IN_ROW_5_sw8[0]));
  DipSwitch IN_ROW_6 (
    .sw1(IN_ROW_6_sw8[7]), .sw2(IN_ROW_6_sw8[6]), .sw3(IN_ROW_6_sw8[5]), .sw4(IN_ROW_6_sw8[4]),
    .sw5(IN_ROW_6_sw8[3]), .sw6(IN_ROW_6_sw8[2]), .sw7(IN_ROW_6_sw8[1]), .sw8(IN_ROW_6_sw8[0]));
  DipSwitch IN_ROW_7 (
    .sw1(IN_ROW_7_sw8[7]), .sw2(IN_ROW_7_sw8[6]), .sw3(IN_ROW_7_sw8[5]), .sw4(IN_ROW_7_sw8[4]),
    .sw5(IN_ROW_7_sw8[3]), .sw6(IN_ROW_7_sw8[2]), .sw7(IN_ROW_7_sw8[1]), .sw8(IN_ROW_7_sw8[0]));
  DipSwitch IN_ROW_8 (
    .sw1(IN_ROW_8_sw8[7]), .sw2(IN_ROW_8_sw8[6]), .sw3(IN_ROW_8_sw8[5]), .sw4(IN_ROW_8_sw8[4]),
    .sw5(IN_ROW_8_sw8[3]), .sw6(IN_ROW_8_sw8[2]), .sw7(IN_ROW_8_sw8[1]), .sw8(IN_ROW_8_sw8[0]));
  Clock CLK (.out(CLK_out));
  and and_1 (and_1_out, CLK_EN, CLK_out);
  // Probe on {IN_ROW_8_sw8, IN_ROW_7_sw8, IN_ROW_6_sw8, IN_ROW_5_sw8, IN_ROW_4_sw8, IN_ROW_3_sw8, IN_ROW_2_sw8, IN_ROW_1_sw8}
  // Probe on cell_grid_1_grid_out
  system_memory system_memory_1 (
    .GRID_IN(cell_grid_1_grid_out),
    .INITIAL_IN({IN_ROW_8_sw8, IN_ROW_7_sw8, IN_ROW_6_sw8, IN_ROW_5_sw8, IN_ROW_4_sw8, IN_ROW_3_sw8, IN_ROW_2_sw8, IN_ROW_1_sw8}),
    .WRITE_ENABLE(1'b1), .LOAD_RUN(LOAD_RUN), .CLK(and_1_out), .RESET(RESET),
    .MEM_OUT(system_memory_1_mem_out));
  DotMatrix #(.inputtype("row"), .matrixcols(8), .matrixrows(8)) INPUT_DISPLAY (
    .row0(system_memory_1_mem_out[7:0]), .row1(system_memory_1_mem_out[15:8]),
    .row2(system_memory_1_mem_out[23:16]), .row3(system_memory_1_mem_out[31:24]),
    .row4(system_memory_1_mem_out[39:32]), .row5(system_memory_1_mem_out[47:40]),
    .row6(system_memory_1_mem_out[55:48]), .row7(system_memory_1_mem_out[63:56]));
  cell_grid cell_grid_1 (.GRID_IN(system_memory_1_mem_out), .GRID_OUT(cell_grid_1_grid_out));
  DotMatrix #(.inputtype("row"), .matrixcols(8), .matrixrows(8)) OUTPUT_DISPLAY (
    .row0(cell_grid_1_grid_out[7:0]), .row1(cell_grid_1_grid_out[15:8]), .row2(cell_grid_1_grid_out[23:16]),
    .row3(cell_grid_1_grid_out[31:24]), .row4(cell_grid_1_grid_out[39:32]),
    .row5(cell_grid_1_grid_out[47:40]), .row6(cell_grid_1_grid_out[55:48]), .row7(cell_grid_1_grid_out[63:56]));

  // Notes on the sheet:
  //   1. Set in your initial value using the DIP switches
  //   2. Set CLK_EN to true and cycle CLK once to load memory
  //   3. Set LOAD_RUN to start running the proces
  //   4. Keep cycling CLK to run through the process
endmodule

module cell_grid (
  input  [63:0] GRID_IN,
  output [63:0] GRID_OUT
);

  wire CELL_0_0_me_e, CELL_0_0_me_s, CELL_0_1_me_e, CELL_0_1_me_s, CELL_0_1_me_w, CELL_0_2_me_e,
       CELL_0_2_me_s, CELL_0_2_me_w, CELL_0_3_me_e, CELL_0_3_me_s, CELL_0_3_me_w, CELL_0_4_me_e,
       CELL_0_4_me_s, CELL_0_4_me_w, CELL_0_5_me_e, CELL_0_5_me_s, CELL_0_5_me_w, CELL_0_6_me_e,
       CELL_0_6_me_s, CELL_0_6_me_w, CELL_0_7_me_s, CELL_0_7_me_w, CELL_1_0_me_e, CELL_1_0_me_n,
       CELL_1_0_me_s, CELL_1_1_me_e, CELL_1_1_me_n, CELL_1_1_me_s, CELL_1_1_me_w, CELL_1_2_me_e,
       CELL_1_2_me_n, CELL_1_2_me_s, CELL_1_2_me_w, CELL_1_3_me_e, CELL_1_3_me_n, CELL_1_3_me_s,
       CELL_1_3_me_w, CELL_1_4_me_e, CELL_1_4_me_n, CELL_1_4_me_s, CELL_1_4_me_w, CELL_1_5_me_e,
       CELL_1_5_me_n, CELL_1_5_me_s, CELL_1_5_me_w, CELL_1_6_me_e, CELL_1_6_me_n, CELL_1_6_me_s,
       CELL_1_6_me_w, CELL_1_7_me_n, CELL_1_7_me_s, CELL_1_7_me_w, CELL_2_0_me_e, CELL_2_0_me_n,
       CELL_2_0_me_s, CELL_2_1_me_e, CELL_2_1_me_n, CELL_2_1_me_s, CELL_2_1_me_w, CELL_2_2_me_e,
       CELL_2_2_me_n, CELL_2_2_me_s, CELL_2_2_me_w, CELL_2_3_me_e, CELL_2_3_me_n, CELL_2_3_me_s,
       CELL_2_3_me_w, CELL_2_4_me_e, CELL_2_4_me_n, CELL_2_4_me_s, CELL_2_4_me_w, CELL_2_5_me_e,
       CELL_2_5_me_n, CELL_2_5_me_s, CELL_2_5_me_w, CELL_2_6_me_e, CELL_2_6_me_n, CELL_2_6_me_s,
       CELL_2_6_me_w, CELL_2_7_me_n, CELL_2_7_me_s, CELL_2_7_me_w, CELL_3_0_me_e, CELL_3_0_me_n,
       CELL_3_0_me_s, CELL_3_1_me_e, CELL_3_1_me_n, CELL_3_1_me_s, CELL_3_1_me_w, CELL_3_2_me_e,
       CELL_3_2_me_n, CELL_3_2_me_s, CELL_3_2_me_w, CELL_3_3_me_e, CELL_3_3_me_n, CELL_3_3_me_s,
       CELL_3_3_me_w, CELL_3_4_me_e, CELL_3_4_me_n, CELL_3_4_me_s, CELL_3_4_me_w, CELL_3_5_me_e,
       CELL_3_5_me_n, CELL_3_5_me_s, CELL_3_5_me_w, CELL_3_6_me_e, CELL_3_6_me_n, CELL_3_6_me_s,
       CELL_3_6_me_w, CELL_3_7_me_n, CELL_3_7_me_s, CELL_3_7_me_w, CELL_4_0_me_e, CELL_4_0_me_n,
       CELL_4_0_me_s, CELL_4_1_me_e, CELL_4_1_me_n, CELL_4_1_me_s, CELL_4_1_me_w, CELL_4_2_me_e,
       CELL_4_2_me_n, CELL_4_2_me_s, CELL_4_2_me_w, CELL_4_3_me_e, CELL_4_3_me_n, CELL_4_3_me_s,
       CELL_4_3_me_w, CELL_4_4_me_e, CELL_4_4_me_n, CELL_4_4_me_s, CELL_4_4_me_w, CELL_4_5_me_e,
       CELL_4_5_me_n, CELL_4_5_me_s, CELL_4_5_me_w, CELL_4_6_me_e, CELL_4_6_me_n, CELL_4_6_me_s,
       CELL_4_6_me_w, CELL_4_7_me_n, CELL_4_7_me_s, CELL_4_7_me_w, CELL_5_0_me_e, CELL_5_0_me_n,
       CELL_5_0_me_s, CELL_5_1_me_e, CELL_5_1_me_n, CELL_5_1_me_s, CELL_5_1_me_w, CELL_5_2_me_e,
       CELL_5_2_me_n, CELL_5_2_me_s, CELL_5_2_me_w, CELL_5_3_me_e, CELL_5_3_me_n, CELL_5_3_me_s,
       CELL_5_3_me_w, CELL_5_4_me_e, CELL_5_4_me_n, CELL_5_4_me_s, CELL_5_4_me_w, CELL_5_5_me_e,
       CELL_5_5_me_n, CELL_5_5_me_s, CELL_5_5_me_w, CELL_5_6_me_e, CELL_5_6_me_n, CELL_5_6_me_s,
       CELL_5_6_me_w, CELL_5_7_me_n, CELL_5_7_me_s, CELL_5_7_me_w, CELL_6_0_me_e, CELL_6_0_me_n,
       CELL_6_0_me_s, CELL_6_1_me_e, CELL_6_1_me_n, CELL_6_1_me_s, CELL_6_1_me_w, CELL_6_2_me_e,
       CELL_6_2_me_n, CELL_6_2_me_s, CELL_6_2_me_w, CELL_6_3_me_e, CELL_6_3_me_n, CELL_6_3_me_s,
       CELL_6_3_me_w, CELL_6_4_me_e, CELL_6_4_me_n, CELL_6_4_me_s, CELL_6_4_me_w, CELL_6_5_me_e,
       CELL_6_5_me_n, CELL_6_5_me_s, CELL_6_5_me_w, CELL_6_6_me_e, CELL_6_6_me_n, CELL_6_6_me_s,
       CELL_6_6_me_w, CELL_6_7_me_n, CELL_6_7_me_s, CELL_6_7_me_w, CELL_7_0_me_e, CELL_7_0_me_n,
       CELL_7_1_me_e, CELL_7_1_me_n, CELL_7_1_me_w, CELL_7_2_me_e, CELL_7_2_me_n, CELL_7_2_me_w,
       CELL_7_3_me_e, CELL_7_3_me_n, CELL_7_3_me_w, CELL_7_4_me_e, CELL_7_4_me_n, CELL_7_4_me_w,
       CELL_7_5_me_e, CELL_7_5_me_n, CELL_7_5_me_w, CELL_7_6_me_e, CELL_7_6_me_n, CELL_7_6_me_w,
       CELL_7_7_me_n, CELL_7_7_me_w;

  single_cell CELL_0_0 (
    .E(CELL_0_1_me_w), .S(CELL_1_0_me_n), .SE(CELL_1_1_me_n), .ME(GRID_IN[0]), .ALIVE(GRID_OUT[0]),
    .ME_S(CELL_0_0_me_s), .ME_E(CELL_0_0_me_e));  // open: NE, N, NW, W, SW, ME_N, ME_W
  single_cell CELL_1_0 (
    .NE(CELL_0_1_me_s), .N(CELL_0_0_me_s), .E(CELL_1_1_me_w), .S(CELL_2_0_me_n), .SE(CELL_2_1_me_n),
    .ME(GRID_IN[8]), .ALIVE(GRID_OUT[8]), .ME_N(CELL_1_0_me_n), .ME_S(CELL_1_0_me_s), .ME_E(CELL_1_0_me_e));  // open: NW, W, SW, ME_W
  single_cell CELL_2_0 (
    .NE(CELL_1_1_me_s), .N(CELL_1_0_me_s), .E(CELL_2_1_me_w), .S(CELL_3_0_me_n), .SE(CELL_3_1_me_n),
    .ME(GRID_IN[16]), .ALIVE(GRID_OUT[16]), .ME_N(CELL_2_0_me_n), .ME_S(CELL_2_0_me_s), .ME_E(CELL_2_0_me_e));  // open: NW, W, SW, ME_W
  single_cell CELL_3_0 (
    .NE(CELL_2_1_me_s), .N(CELL_2_0_me_s), .E(CELL_3_1_me_w), .S(CELL_4_0_me_n), .SE(CELL_4_1_me_n),
    .ME(GRID_IN[24]), .ALIVE(GRID_OUT[24]), .ME_N(CELL_3_0_me_n), .ME_S(CELL_3_0_me_s), .ME_E(CELL_3_0_me_e));  // open: NW, W, SW, ME_W
  single_cell CELL_4_0 (
    .NE(CELL_3_1_me_s), .N(CELL_3_0_me_s), .E(CELL_4_1_me_w), .S(CELL_5_0_me_n), .SE(CELL_5_1_me_n),
    .ME(GRID_IN[32]), .ALIVE(GRID_OUT[32]), .ME_N(CELL_4_0_me_n), .ME_S(CELL_4_0_me_s), .ME_E(CELL_4_0_me_e));  // open: NW, W, SW, ME_W
  single_cell CELL_5_0 (
    .NE(CELL_4_1_me_s), .N(CELL_4_0_me_s), .E(CELL_5_1_me_w), .S(CELL_6_0_me_n), .SE(CELL_6_1_me_n),
    .ME(GRID_IN[40]), .ALIVE(GRID_OUT[40]), .ME_N(CELL_5_0_me_n), .ME_S(CELL_5_0_me_s), .ME_E(CELL_5_0_me_e));  // open: NW, W, SW, ME_W
  single_cell CELL_6_0 (
    .NE(CELL_5_1_me_s), .N(CELL_5_0_me_s), .E(CELL_6_1_me_w), .S(CELL_7_0_me_n), .SE(CELL_7_1_me_n),
    .ME(GRID_IN[48]), .ALIVE(GRID_OUT[48]), .ME_N(CELL_6_0_me_n), .ME_S(CELL_6_0_me_s), .ME_E(CELL_6_0_me_e));  // open: NW, W, SW, ME_W
  single_cell CELL_7_0 (
    .NE(CELL_6_1_me_s), .N(CELL_6_0_me_s), .E(CELL_7_1_me_w), .ME(GRID_IN[56]), .ALIVE(GRID_OUT[56]),
    .ME_N(CELL_7_0_me_n), .ME_E(CELL_7_0_me_e));  // open: NW, W, SW, S, SE, ME_S, ME_W
  single_cell CELL_0_1 (
    .W(CELL_0_0_me_e), .E(CELL_0_2_me_w), .SW(CELL_1_0_me_n), .S(CELL_1_1_me_n), .SE(CELL_1_2_me_n),
    .ME(GRID_IN[1]), .ALIVE(GRID_OUT[1]), .ME_S(CELL_0_1_me_s), .ME_E(CELL_0_1_me_e), .ME_W(CELL_0_1_me_w));  // open: NE, N, NW, ME_N
  single_cell CELL_1_1 (
    .NE(CELL_0_2_me_s), .N(CELL_0_1_me_s), .NW(CELL_0_0_me_s), .W(CELL_1_0_me_e), .E(CELL_1_2_me_w),
    .SW(CELL_2_0_me_n), .S(CELL_2_1_me_n), .SE(CELL_2_2_me_n), .ME(GRID_IN[9]), .ALIVE(GRID_OUT[9]),
    .ME_N(CELL_1_1_me_n), .ME_S(CELL_1_1_me_s), .ME_E(CELL_1_1_me_e), .ME_W(CELL_1_1_me_w));
  single_cell CELL_2_1 (
    .NE(CELL_1_2_me_s), .N(CELL_1_1_me_s), .NW(CELL_1_0_me_s), .W(CELL_2_0_me_e), .E(CELL_2_2_me_w),
    .SW(CELL_3_0_me_n), .S(CELL_3_1_me_n), .SE(CELL_3_2_me_n), .ME(GRID_IN[17]), .ALIVE(GRID_OUT[17]),
    .ME_N(CELL_2_1_me_n), .ME_S(CELL_2_1_me_s), .ME_E(CELL_2_1_me_e), .ME_W(CELL_2_1_me_w));
  single_cell CELL_3_1 (
    .NE(CELL_2_2_me_s), .N(CELL_2_1_me_s), .NW(CELL_2_0_me_s), .W(CELL_3_0_me_e), .E(CELL_3_2_me_w),
    .SW(CELL_4_0_me_n), .S(CELL_4_1_me_n), .SE(CELL_4_2_me_n), .ME(GRID_IN[25]), .ALIVE(GRID_OUT[25]),
    .ME_N(CELL_3_1_me_n), .ME_S(CELL_3_1_me_s), .ME_E(CELL_3_1_me_e), .ME_W(CELL_3_1_me_w));
  single_cell CELL_4_1 (
    .NE(CELL_3_2_me_s), .N(CELL_3_1_me_s), .NW(CELL_3_0_me_s), .W(CELL_4_0_me_e), .E(CELL_4_2_me_w),
    .SW(CELL_5_0_me_n), .S(CELL_5_1_me_n), .SE(CELL_5_2_me_n), .ME(GRID_IN[33]), .ALIVE(GRID_OUT[33]),
    .ME_N(CELL_4_1_me_n), .ME_S(CELL_4_1_me_s), .ME_E(CELL_4_1_me_e), .ME_W(CELL_4_1_me_w));
  single_cell CELL_5_1 (
    .NE(CELL_4_2_me_s), .N(CELL_4_1_me_s), .NW(CELL_4_0_me_s), .W(CELL_5_0_me_e), .E(CELL_5_2_me_w),
    .SW(CELL_6_0_me_n), .S(CELL_6_1_me_n), .SE(CELL_6_2_me_n), .ME(GRID_IN[41]), .ALIVE(GRID_OUT[41]),
    .ME_N(CELL_5_1_me_n), .ME_S(CELL_5_1_me_s), .ME_E(CELL_5_1_me_e), .ME_W(CELL_5_1_me_w));
  single_cell CELL_6_1 (
    .NE(CELL_5_2_me_s), .N(CELL_5_1_me_s), .NW(CELL_5_0_me_s), .W(CELL_6_0_me_e), .E(CELL_6_2_me_w),
    .SW(CELL_7_0_me_n), .S(CELL_7_1_me_n), .SE(CELL_7_2_me_n), .ME(GRID_IN[49]), .ALIVE(GRID_OUT[49]),
    .ME_N(CELL_6_1_me_n), .ME_S(CELL_6_1_me_s), .ME_E(CELL_6_1_me_e), .ME_W(CELL_6_1_me_w));
  single_cell CELL_7_1 (
    .NE(CELL_6_2_me_s), .N(CELL_6_1_me_s), .NW(CELL_6_0_me_s), .W(CELL_7_0_me_e), .E(CELL_7_2_me_w),
    .ME(GRID_IN[57]), .ALIVE(GRID_OUT[57]), .ME_N(CELL_7_1_me_n), .ME_E(CELL_7_1_me_e), .ME_W(CELL_7_1_me_w));  // open: SW, S, SE, ME_S
  single_cell CELL_0_2 (
    .W(CELL_0_1_me_e), .E(CELL_0_3_me_w), .SW(CELL_1_1_me_n), .S(CELL_1_2_me_n), .SE(CELL_1_3_me_n),
    .ME(GRID_IN[2]), .ALIVE(GRID_OUT[2]), .ME_S(CELL_0_2_me_s), .ME_E(CELL_0_2_me_e), .ME_W(CELL_0_2_me_w));  // open: NE, N, NW, ME_N
  single_cell CELL_1_2 (
    .NE(CELL_0_3_me_s), .N(CELL_0_2_me_s), .NW(CELL_0_1_me_s), .W(CELL_1_1_me_e), .E(CELL_1_3_me_w),
    .SW(CELL_2_1_me_n), .S(CELL_2_2_me_n), .SE(CELL_2_3_me_n), .ME(GRID_IN[10]), .ALIVE(GRID_OUT[10]),
    .ME_N(CELL_1_2_me_n), .ME_S(CELL_1_2_me_s), .ME_E(CELL_1_2_me_e), .ME_W(CELL_1_2_me_w));
  single_cell CELL_2_2 (
    .NE(CELL_1_3_me_s), .N(CELL_1_2_me_s), .NW(CELL_1_1_me_s), .W(CELL_2_1_me_e), .E(CELL_2_3_me_w),
    .SW(CELL_3_1_me_n), .S(CELL_3_2_me_n), .SE(CELL_3_3_me_n), .ME(GRID_IN[18]), .ALIVE(GRID_OUT[18]),
    .ME_N(CELL_2_2_me_n), .ME_S(CELL_2_2_me_s), .ME_E(CELL_2_2_me_e), .ME_W(CELL_2_2_me_w));
  single_cell CELL_3_2 (
    .NE(CELL_2_3_me_s), .N(CELL_2_2_me_s), .NW(CELL_2_1_me_s), .W(CELL_3_1_me_e), .E(CELL_3_3_me_w),
    .SW(CELL_4_1_me_n), .S(CELL_4_2_me_n), .SE(CELL_4_3_me_n), .ME(GRID_IN[26]), .ALIVE(GRID_OUT[26]),
    .ME_N(CELL_3_2_me_n), .ME_S(CELL_3_2_me_s), .ME_E(CELL_3_2_me_e), .ME_W(CELL_3_2_me_w));
  single_cell CELL_4_2 (
    .NE(CELL_3_3_me_s), .N(CELL_3_2_me_s), .NW(CELL_3_1_me_s), .W(CELL_4_1_me_e), .E(CELL_4_3_me_w),
    .SW(CELL_5_1_me_n), .S(CELL_5_2_me_n), .SE(CELL_5_3_me_n), .ME(GRID_IN[34]), .ALIVE(GRID_OUT[34]),
    .ME_N(CELL_4_2_me_n), .ME_S(CELL_4_2_me_s), .ME_E(CELL_4_2_me_e), .ME_W(CELL_4_2_me_w));
  single_cell CELL_5_2 (
    .NE(CELL_4_3_me_s), .N(CELL_4_2_me_s), .NW(CELL_4_1_me_s), .W(CELL_5_1_me_e), .E(CELL_5_3_me_w),
    .SW(CELL_6_1_me_n), .S(CELL_6_2_me_n), .SE(CELL_6_3_me_n), .ME(GRID_IN[42]), .ALIVE(GRID_OUT[42]),
    .ME_N(CELL_5_2_me_n), .ME_S(CELL_5_2_me_s), .ME_E(CELL_5_2_me_e), .ME_W(CELL_5_2_me_w));
  single_cell CELL_6_2 (
    .NE(CELL_5_3_me_s), .N(CELL_5_2_me_s), .NW(CELL_5_1_me_s), .W(CELL_6_1_me_e), .E(CELL_6_3_me_w),
    .SW(CELL_7_1_me_n), .S(CELL_7_2_me_n), .SE(CELL_7_3_me_n), .ME(GRID_IN[50]), .ALIVE(GRID_OUT[50]),
    .ME_N(CELL_6_2_me_n), .ME_S(CELL_6_2_me_s), .ME_E(CELL_6_2_me_e), .ME_W(CELL_6_2_me_w));
  single_cell CELL_7_2 (
    .NE(CELL_6_3_me_s), .N(CELL_6_2_me_s), .NW(CELL_6_1_me_s), .W(CELL_7_1_me_e), .E(CELL_7_3_me_w),
    .ME(GRID_IN[58]), .ALIVE(GRID_OUT[58]), .ME_N(CELL_7_2_me_n), .ME_E(CELL_7_2_me_e), .ME_W(CELL_7_2_me_w));  // open: SW, S, SE, ME_S
  single_cell CELL_0_3 (
    .W(CELL_0_2_me_e), .E(CELL_0_4_me_w), .SW(CELL_1_2_me_n), .S(CELL_1_3_me_n), .SE(CELL_1_4_me_n),
    .ME(GRID_IN[3]), .ALIVE(GRID_OUT[3]), .ME_S(CELL_0_3_me_s), .ME_E(CELL_0_3_me_e), .ME_W(CELL_0_3_me_w));  // open: NE, N, NW, ME_N
  single_cell CELL_1_3 (
    .NE(CELL_0_4_me_s), .N(CELL_0_3_me_s), .NW(CELL_0_2_me_s), .W(CELL_1_2_me_e), .E(CELL_1_4_me_w),
    .SW(CELL_2_2_me_n), .S(CELL_2_3_me_n), .SE(CELL_2_4_me_n), .ME(GRID_IN[11]), .ALIVE(GRID_OUT[11]),
    .ME_N(CELL_1_3_me_n), .ME_S(CELL_1_3_me_s), .ME_E(CELL_1_3_me_e), .ME_W(CELL_1_3_me_w));
  single_cell CELL_2_3 (
    .NE(CELL_1_4_me_s), .N(CELL_1_3_me_s), .NW(CELL_1_2_me_s), .W(CELL_2_2_me_e), .E(CELL_2_4_me_w),
    .SW(CELL_3_2_me_n), .S(CELL_3_3_me_n), .SE(CELL_3_4_me_n), .ME(GRID_IN[19]), .ALIVE(GRID_OUT[19]),
    .ME_N(CELL_2_3_me_n), .ME_S(CELL_2_3_me_s), .ME_E(CELL_2_3_me_e), .ME_W(CELL_2_3_me_w));
  single_cell CELL_3_3 (
    .NE(CELL_2_4_me_s), .N(CELL_2_3_me_s), .NW(CELL_2_2_me_s), .W(CELL_3_2_me_e), .E(CELL_3_4_me_w),
    .SW(CELL_4_2_me_n), .S(CELL_4_3_me_n), .SE(CELL_4_4_me_n), .ME(GRID_IN[27]), .ALIVE(GRID_OUT[27]),
    .ME_N(CELL_3_3_me_n), .ME_S(CELL_3_3_me_s), .ME_E(CELL_3_3_me_e), .ME_W(CELL_3_3_me_w));
  single_cell CELL_4_3 (
    .NE(CELL_3_4_me_s), .N(CELL_3_3_me_s), .NW(CELL_3_2_me_s), .W(CELL_4_2_me_e), .E(CELL_4_4_me_w),
    .SW(CELL_5_2_me_n), .S(CELL_5_3_me_n), .SE(CELL_5_4_me_n), .ME(GRID_IN[35]), .ALIVE(GRID_OUT[35]),
    .ME_N(CELL_4_3_me_n), .ME_S(CELL_4_3_me_s), .ME_E(CELL_4_3_me_e), .ME_W(CELL_4_3_me_w));
  single_cell CELL_5_3 (
    .NE(CELL_4_4_me_s), .N(CELL_4_3_me_s), .NW(CELL_4_2_me_s), .W(CELL_5_2_me_e), .E(CELL_5_4_me_w),
    .SW(CELL_6_2_me_n), .S(CELL_6_3_me_n), .SE(CELL_6_4_me_n), .ME(GRID_IN[43]), .ALIVE(GRID_OUT[43]),
    .ME_N(CELL_5_3_me_n), .ME_S(CELL_5_3_me_s), .ME_E(CELL_5_3_me_e), .ME_W(CELL_5_3_me_w));
  single_cell CELL_6_3 (
    .NE(CELL_5_4_me_s), .N(CELL_5_3_me_s), .NW(CELL_5_2_me_s), .W(CELL_6_2_me_e), .E(CELL_6_4_me_w),
    .SW(CELL_7_2_me_n), .S(CELL_7_3_me_n), .SE(CELL_7_4_me_n), .ME(GRID_IN[51]), .ALIVE(GRID_OUT[51]),
    .ME_N(CELL_6_3_me_n), .ME_S(CELL_6_3_me_s), .ME_E(CELL_6_3_me_e), .ME_W(CELL_6_3_me_w));
  single_cell CELL_7_3 (
    .NE(CELL_6_4_me_s), .N(CELL_6_3_me_s), .NW(CELL_6_2_me_s), .W(CELL_7_2_me_e), .E(CELL_7_4_me_w),
    .ME(GRID_IN[59]), .ALIVE(GRID_OUT[59]), .ME_N(CELL_7_3_me_n), .ME_E(CELL_7_3_me_e), .ME_W(CELL_7_3_me_w));  // open: SW, S, SE, ME_S
  single_cell CELL_0_4 (
    .W(CELL_0_3_me_e), .E(CELL_0_5_me_w), .SW(CELL_1_3_me_n), .S(CELL_1_4_me_n), .SE(CELL_1_5_me_n),
    .ME(GRID_IN[4]), .ALIVE(GRID_OUT[4]), .ME_S(CELL_0_4_me_s), .ME_E(CELL_0_4_me_e), .ME_W(CELL_0_4_me_w));  // open: NE, N, NW, ME_N
  single_cell CELL_1_4 (
    .NE(CELL_0_5_me_s), .N(CELL_0_4_me_s), .NW(CELL_0_3_me_s), .W(CELL_1_3_me_e), .E(CELL_1_5_me_w),
    .SW(CELL_2_3_me_n), .S(CELL_2_4_me_n), .SE(CELL_2_5_me_n), .ME(GRID_IN[12]), .ALIVE(GRID_OUT[12]),
    .ME_N(CELL_1_4_me_n), .ME_S(CELL_1_4_me_s), .ME_E(CELL_1_4_me_e), .ME_W(CELL_1_4_me_w));
  single_cell CELL_2_4 (
    .NE(CELL_1_5_me_s), .N(CELL_1_4_me_s), .NW(CELL_1_3_me_s), .W(CELL_2_3_me_e), .E(CELL_2_5_me_w),
    .SW(CELL_3_3_me_n), .S(CELL_3_4_me_n), .SE(CELL_3_5_me_n), .ME(GRID_IN[20]), .ALIVE(GRID_OUT[20]),
    .ME_N(CELL_2_4_me_n), .ME_S(CELL_2_4_me_s), .ME_E(CELL_2_4_me_e), .ME_W(CELL_2_4_me_w));
  single_cell CELL_3_4 (
    .NE(CELL_2_5_me_s), .N(CELL_2_4_me_s), .NW(CELL_2_3_me_s), .W(CELL_3_3_me_e), .E(CELL_3_5_me_w),
    .SW(CELL_4_3_me_n), .S(CELL_4_4_me_n), .SE(CELL_4_5_me_n), .ME(GRID_IN[28]), .ALIVE(GRID_OUT[28]),
    .ME_N(CELL_3_4_me_n), .ME_S(CELL_3_4_me_s), .ME_E(CELL_3_4_me_e), .ME_W(CELL_3_4_me_w));
  single_cell CELL_4_4 (
    .NE(CELL_3_5_me_s), .N(CELL_3_4_me_s), .NW(CELL_3_3_me_s), .W(CELL_4_3_me_e), .E(CELL_4_5_me_w),
    .SW(CELL_5_3_me_n), .S(CELL_5_4_me_n), .SE(CELL_5_5_me_n), .ME(GRID_IN[36]), .ALIVE(GRID_OUT[36]),
    .ME_N(CELL_4_4_me_n), .ME_S(CELL_4_4_me_s), .ME_E(CELL_4_4_me_e), .ME_W(CELL_4_4_me_w));
  single_cell CELL_5_4 (
    .NE(CELL_4_5_me_s), .N(CELL_4_4_me_s), .NW(CELL_4_3_me_s), .W(CELL_5_3_me_e), .E(CELL_5_5_me_w),
    .SW(CELL_6_3_me_n), .S(CELL_6_4_me_n), .SE(CELL_6_5_me_n), .ME(GRID_IN[44]), .ALIVE(GRID_OUT[44]),
    .ME_N(CELL_5_4_me_n), .ME_S(CELL_5_4_me_s), .ME_E(CELL_5_4_me_e), .ME_W(CELL_5_4_me_w));
  single_cell CELL_6_4 (
    .NE(CELL_5_5_me_s), .N(CELL_5_4_me_s), .NW(CELL_5_3_me_s), .W(CELL_6_3_me_e), .E(CELL_6_5_me_w),
    .SW(CELL_7_3_me_n), .S(CELL_7_4_me_n), .SE(CELL_7_5_me_n), .ME(GRID_IN[52]), .ALIVE(GRID_OUT[52]),
    .ME_N(CELL_6_4_me_n), .ME_S(CELL_6_4_me_s), .ME_E(CELL_6_4_me_e), .ME_W(CELL_6_4_me_w));
  single_cell CELL_7_4 (
    .NE(CELL_6_5_me_s), .N(CELL_6_4_me_s), .NW(CELL_6_3_me_s), .W(CELL_7_3_me_e), .E(CELL_7_5_me_w),
    .ME(GRID_IN[60]), .ALIVE(GRID_OUT[60]), .ME_N(CELL_7_4_me_n), .ME_E(CELL_7_4_me_e), .ME_W(CELL_7_4_me_w));  // open: SW, S, SE, ME_S
  single_cell CELL_0_5 (
    .W(CELL_0_4_me_e), .E(CELL_0_6_me_w), .SW(CELL_1_4_me_n), .S(CELL_1_5_me_n), .SE(CELL_1_6_me_n),
    .ME(GRID_IN[5]), .ALIVE(GRID_OUT[5]), .ME_S(CELL_0_5_me_s), .ME_E(CELL_0_5_me_e), .ME_W(CELL_0_5_me_w));  // open: NE, N, NW, ME_N
  single_cell CELL_1_5 (
    .NE(CELL_0_6_me_s), .N(CELL_0_5_me_s), .NW(CELL_0_4_me_s), .W(CELL_1_4_me_e), .E(CELL_1_6_me_w),
    .SW(CELL_2_4_me_n), .S(CELL_2_5_me_n), .SE(CELL_2_6_me_n), .ME(GRID_IN[13]), .ALIVE(GRID_OUT[13]),
    .ME_N(CELL_1_5_me_n), .ME_S(CELL_1_5_me_s), .ME_E(CELL_1_5_me_e), .ME_W(CELL_1_5_me_w));
  single_cell CELL_2_5 (
    .NE(CELL_1_6_me_s), .N(CELL_1_5_me_s), .NW(CELL_1_4_me_s), .W(CELL_2_4_me_e), .E(CELL_2_6_me_w),
    .SW(CELL_3_4_me_n), .S(CELL_3_5_me_n), .SE(CELL_3_6_me_n), .ME(GRID_IN[21]), .ALIVE(GRID_OUT[21]),
    .ME_N(CELL_2_5_me_n), .ME_S(CELL_2_5_me_s), .ME_E(CELL_2_5_me_e), .ME_W(CELL_2_5_me_w));
  single_cell CELL_3_5 (
    .NE(CELL_2_6_me_s), .N(CELL_2_5_me_s), .NW(CELL_2_4_me_s), .W(CELL_3_4_me_e), .E(CELL_3_6_me_w),
    .SW(CELL_4_4_me_n), .S(CELL_4_5_me_n), .SE(CELL_4_6_me_n), .ME(GRID_IN[29]), .ALIVE(GRID_OUT[29]),
    .ME_N(CELL_3_5_me_n), .ME_S(CELL_3_5_me_s), .ME_E(CELL_3_5_me_e), .ME_W(CELL_3_5_me_w));
  single_cell CELL_4_5 (
    .NE(CELL_3_6_me_s), .N(CELL_3_5_me_s), .NW(CELL_3_4_me_s), .W(CELL_4_4_me_e), .E(CELL_4_6_me_w),
    .SW(CELL_5_4_me_n), .S(CELL_5_5_me_n), .SE(CELL_5_6_me_n), .ME(GRID_IN[37]), .ALIVE(GRID_OUT[37]),
    .ME_N(CELL_4_5_me_n), .ME_S(CELL_4_5_me_s), .ME_E(CELL_4_5_me_e), .ME_W(CELL_4_5_me_w));
  single_cell CELL_5_5 (
    .NE(CELL_4_6_me_s), .N(CELL_4_5_me_s), .NW(CELL_4_4_me_s), .W(CELL_5_4_me_e), .E(CELL_5_6_me_w),
    .SW(CELL_6_4_me_n), .S(CELL_6_5_me_n), .SE(CELL_6_6_me_n), .ME(GRID_IN[45]), .ALIVE(GRID_OUT[45]),
    .ME_N(CELL_5_5_me_n), .ME_S(CELL_5_5_me_s), .ME_E(CELL_5_5_me_e), .ME_W(CELL_5_5_me_w));
  single_cell CELL_6_5 (
    .NE(CELL_5_6_me_s), .N(CELL_5_5_me_s), .NW(CELL_5_4_me_s), .W(CELL_6_4_me_e), .E(CELL_6_6_me_w),
    .SW(CELL_7_4_me_n), .S(CELL_7_5_me_n), .SE(CELL_7_6_me_n), .ME(GRID_IN[53]), .ALIVE(GRID_OUT[53]),
    .ME_N(CELL_6_5_me_n), .ME_S(CELL_6_5_me_s), .ME_E(CELL_6_5_me_e), .ME_W(CELL_6_5_me_w));
  single_cell CELL_7_5 (
    .NE(CELL_6_6_me_s), .N(CELL_6_5_me_s), .NW(CELL_6_4_me_s), .W(CELL_7_4_me_e), .E(CELL_7_6_me_w),
    .ME(GRID_IN[61]), .ALIVE(GRID_OUT[61]), .ME_N(CELL_7_5_me_n), .ME_E(CELL_7_5_me_e), .ME_W(CELL_7_5_me_w));  // open: SW, S, SE, ME_S
  single_cell CELL_0_6 (
    .W(CELL_0_5_me_e), .E(CELL_0_7_me_w), .SW(CELL_1_5_me_n), .S(CELL_1_6_me_n), .SE(CELL_1_7_me_n),
    .ME(GRID_IN[6]), .ALIVE(GRID_OUT[6]), .ME_S(CELL_0_6_me_s), .ME_E(CELL_0_6_me_e), .ME_W(CELL_0_6_me_w));  // open: NE, N, NW, ME_N
  single_cell CELL_1_6 (
    .NE(CELL_0_7_me_s), .N(CELL_0_6_me_s), .NW(CELL_0_5_me_s), .W(CELL_1_5_me_e), .E(CELL_1_7_me_w),
    .SW(CELL_2_5_me_n), .S(CELL_2_6_me_n), .SE(CELL_2_7_me_n), .ME(GRID_IN[14]), .ALIVE(GRID_OUT[14]),
    .ME_N(CELL_1_6_me_n), .ME_S(CELL_1_6_me_s), .ME_E(CELL_1_6_me_e), .ME_W(CELL_1_6_me_w));
  single_cell CELL_2_6 (
    .NE(CELL_1_7_me_s), .N(CELL_1_6_me_s), .NW(CELL_1_5_me_s), .W(CELL_2_5_me_e), .E(CELL_2_7_me_w),
    .SW(CELL_3_5_me_n), .S(CELL_3_6_me_n), .SE(CELL_3_7_me_n), .ME(GRID_IN[22]), .ALIVE(GRID_OUT[22]),
    .ME_N(CELL_2_6_me_n), .ME_S(CELL_2_6_me_s), .ME_E(CELL_2_6_me_e), .ME_W(CELL_2_6_me_w));
  single_cell CELL_3_6 (
    .NE(CELL_2_7_me_s), .N(CELL_2_6_me_s), .NW(CELL_2_5_me_s), .W(CELL_3_5_me_e), .E(CELL_3_7_me_w),
    .SW(CELL_4_5_me_n), .S(CELL_4_6_me_n), .SE(CELL_4_7_me_n), .ME(GRID_IN[30]), .ALIVE(GRID_OUT[30]),
    .ME_N(CELL_3_6_me_n), .ME_S(CELL_3_6_me_s), .ME_E(CELL_3_6_me_e), .ME_W(CELL_3_6_me_w));
  single_cell CELL_4_6 (
    .NE(CELL_3_7_me_s), .N(CELL_3_6_me_s), .NW(CELL_3_5_me_s), .W(CELL_4_5_me_e), .E(CELL_4_7_me_w),
    .SW(CELL_5_5_me_n), .S(CELL_5_6_me_n), .SE(CELL_5_7_me_n), .ME(GRID_IN[38]), .ALIVE(GRID_OUT[38]),
    .ME_N(CELL_4_6_me_n), .ME_S(CELL_4_6_me_s), .ME_E(CELL_4_6_me_e), .ME_W(CELL_4_6_me_w));
  single_cell CELL_5_6 (
    .NE(CELL_4_7_me_s), .N(CELL_4_6_me_s), .NW(CELL_4_5_me_s), .W(CELL_5_5_me_e), .E(CELL_5_7_me_w),
    .SW(CELL_6_5_me_n), .S(CELL_6_6_me_n), .SE(CELL_6_7_me_n), .ME(GRID_IN[46]), .ALIVE(GRID_OUT[46]),
    .ME_N(CELL_5_6_me_n), .ME_S(CELL_5_6_me_s), .ME_E(CELL_5_6_me_e), .ME_W(CELL_5_6_me_w));
  single_cell CELL_6_6 (
    .NE(CELL_5_7_me_s), .N(CELL_5_6_me_s), .NW(CELL_5_5_me_s), .W(CELL_6_5_me_e), .E(CELL_6_7_me_w),
    .SW(CELL_7_5_me_n), .S(CELL_7_6_me_n), .SE(CELL_7_7_me_n), .ME(GRID_IN[54]), .ALIVE(GRID_OUT[54]),
    .ME_N(CELL_6_6_me_n), .ME_S(CELL_6_6_me_s), .ME_E(CELL_6_6_me_e), .ME_W(CELL_6_6_me_w));
  single_cell CELL_7_6 (
    .NE(CELL_6_7_me_s), .N(CELL_6_6_me_s), .NW(CELL_6_5_me_s), .W(CELL_7_5_me_e), .E(CELL_7_7_me_w),
    .ME(GRID_IN[62]), .ALIVE(GRID_OUT[62]), .ME_N(CELL_7_6_me_n), .ME_E(CELL_7_6_me_e), .ME_W(CELL_7_6_me_w));  // open: SW, S, SE, ME_S
  single_cell CELL_0_7 (
    .W(CELL_0_6_me_e), .SW(CELL_1_6_me_n), .S(CELL_1_7_me_n), .ME(GRID_IN[7]), .ALIVE(GRID_OUT[7]),
    .ME_S(CELL_0_7_me_s), .ME_W(CELL_0_7_me_w));  // open: NE, N, NW, E, SE, ME_N, ME_E
  single_cell CELL_1_7 (
    .N(CELL_0_7_me_s), .NW(CELL_0_6_me_s), .W(CELL_1_6_me_e), .SW(CELL_2_6_me_n), .S(CELL_2_7_me_n),
    .ME(GRID_IN[15]), .ALIVE(GRID_OUT[15]), .ME_N(CELL_1_7_me_n), .ME_S(CELL_1_7_me_s), .ME_W(CELL_1_7_me_w));  // open: NE, E, SE, ME_E
  single_cell CELL_2_7 (
    .N(CELL_1_7_me_s), .NW(CELL_1_6_me_s), .W(CELL_2_6_me_e), .SW(CELL_3_6_me_n), .S(CELL_3_7_me_n),
    .ME(GRID_IN[23]), .ALIVE(GRID_OUT[23]), .ME_N(CELL_2_7_me_n), .ME_S(CELL_2_7_me_s), .ME_W(CELL_2_7_me_w));  // open: NE, E, SE, ME_E
  single_cell CELL_3_7 (
    .N(CELL_2_7_me_s), .NW(CELL_2_6_me_s), .W(CELL_3_6_me_e), .SW(CELL_4_6_me_n), .S(CELL_4_7_me_n),
    .ME(GRID_IN[31]), .ALIVE(GRID_OUT[31]), .ME_N(CELL_3_7_me_n), .ME_S(CELL_3_7_me_s), .ME_W(CELL_3_7_me_w));  // open: NE, E, SE, ME_E
  single_cell CELL_4_7 (
    .N(CELL_3_7_me_s), .NW(CELL_3_6_me_s), .W(CELL_4_6_me_e), .SW(CELL_5_6_me_n), .S(CELL_5_7_me_n),
    .ME(GRID_IN[39]), .ALIVE(GRID_OUT[39]), .ME_N(CELL_4_7_me_n), .ME_S(CELL_4_7_me_s), .ME_W(CELL_4_7_me_w));  // open: NE, E, SE, ME_E
  single_cell CELL_5_7 (
    .N(CELL_4_7_me_s), .NW(CELL_4_6_me_s), .W(CELL_5_6_me_e), .SW(CELL_6_6_me_n), .S(CELL_6_7_me_n),
    .ME(GRID_IN[47]), .ALIVE(GRID_OUT[47]), .ME_N(CELL_5_7_me_n), .ME_S(CELL_5_7_me_s), .ME_W(CELL_5_7_me_w));  // open: NE, E, SE, ME_E
  single_cell CELL_6_7 (
    .N(CELL_5_7_me_s), .NW(CELL_5_6_me_s), .W(CELL_6_6_me_e), .SW(CELL_7_6_me_n), .S(CELL_7_7_me_n),
    .ME(GRID_IN[55]), .ALIVE(GRID_OUT[55]), .ME_N(CELL_6_7_me_n), .ME_S(CELL_6_7_me_s), .ME_W(CELL_6_7_me_w));  // open: NE, E, SE, ME_E
  single_cell CELL_7_7 (
    .N(CELL_6_7_me_s), .NW(CELL_6_6_me_s), .W(CELL_7_6_me_e), .ME(GRID_IN[63]), .ALIVE(GRID_OUT[63]),
    .ME_N(CELL_7_7_me_n), .ME_W(CELL_7_7_me_w));  // open: NE, E, SW, S, SE, ME_S, ME_E
endmodule

module system_memory (
  input  [63:0] GRID_IN,
  input  [63:0] INITIAL_IN,
  input  WRITE_ENABLE,
  input  LOAD_RUN,
  input  CLK,
  input  RESET,
  output [63:0] MEM_OUT
);

  wire [63:0] multiplexer_1_out;

  Multiplexer #(.width(64)) multiplexer_1 (.in0(INITIAL_IN), .in1(GRID_IN), .out(multiplexer_1_out), .sel(LOAD_RUN));
  Register #(.width(64)) register_1 (.D(multiplexer_1_out), .en(WRITE_ENABLE), .clk(CLK), .Q(MEM_OUT), .clr(RESET));

  // Notes on the sheet:
  //   Loads in and stores memory in register. When in load mode, data to load is passed through to help with debugging
endmodule

module fully_combined_memory (
  input  RST,
  input  RUN_MODE,
  input  LOAD_MODE,
  input  CLK,
  input  DATA_IN,
  input  [63:0] GRID_IN,
  input  OUTPUT_MODE,
  output [63:0] DATA,
  output [63:0] PARALEL_OUT,
  output SERIAL_OUT
);

  wire or_1_out;

  // Shift_Register #(.length(64)) shift_register_1: pin names not known; wires that end beside it: RST, RUN_MODE, LOAD_MODE, CLK, DATA_IN, GRID_IN[63], GRID_IN[62], GRID_IN[61], GRID_IN[60], GRID_IN[59], GRID_IN[58], GRID_IN[57], GRID_IN[56], GRID_IN[55], GRID_IN[54], GRID_IN[53], GRID_IN[52], DATA[63], DATA[62], DATA[61], DATA[60], DATA[59], DATA[58], DATA[57], DATA[56], DATA[55], DATA[54], DATA[53], DATA[52]
  // Probe on DATA
  or or_1 (or_1_out, LOAD_MODE, OUTPUT_MODE);
  // Shift_Register #(.length(64)) shift_register_2: pin names not known; wires that end beside it: RST, RUN_MODE, or_1_out, CLK, DATA_IN, GRID_IN[63], GRID_IN[62], GRID_IN[61], GRID_IN[60], GRID_IN[59], GRID_IN[58], GRID_IN[57], GRID_IN[56], GRID_IN[55], GRID_IN[54], GRID_IN[53], GRID_IN[52], PARALEL_OUT[63], PARALEL_OUT[62], PARALEL_OUT[61], PARALEL_OUT[60], PARALEL_OUT[59], PARALEL_OUT[58], PARALEL_OUT[57], PARALEL_OUT[56], PARALEL_OUT[55], PARALEL_OUT[54], PARALEL_OUT[53], PARALEL_OUT[52]

  assign SERIAL_OUT = PARALEL_OUT[0];

  // Notes on the sheet:
  //   1. Toggle reset to restart system
  //   2. Enable EN and clock to shift data in
  //   Since the shift register has parallel load support, we can use it as the memory instead of a separate set of registers
  //   We need 2 shift registers so that shifting out does not wipe internal data
endmodule

module main_shift_based_v3 (
  input  DATA_IN,
  input  [1:0] MODE,
  input  RESET,
  output DATA_OUT
);

  wire and_1_out, CLK_out, decoder_1_out0, decoder_1_out1, decoder_1_out2, decoder_1_out3, not_1_out;
  wire [7:0] cell_grid_1_grid_out, cell_grid_1_grid_out_2, cell_grid_1_grid_out_3, cell_grid_1_grid_out_4,
       cell_grid_1_grid_out_5, cell_grid_1_grid_out_6, cell_grid_1_grid_out_7, cell_grid_1_grid_out_8;
  wire [63:0] fully_combined_memory_1_data, fully_combined_memory_1_paralel_out;

  Decoder #(.select(2)) decoder_1 (
    .out0(decoder_1_out0), .out1(decoder_1_out1), .out2(decoder_1_out2), .out3(decoder_1_out3), .sel(MODE));  // open: en
  Clock CLK (.out(CLK_out));
  not not_1 (not_1_out, decoder_1_out0);
  and and_1 (and_1_out, not_1_out, CLK_out);
  // Probe on fully_combined_memory_1_data
  fully_combined_memory fully_combined_memory_1 (
    .OUTPUT_MODE(decoder_1_out3),
    .GRID_IN({cell_grid_1_grid_out_8, cell_grid_1_grid_out_7, cell_grid_1_grid_out_6, cell_grid_1_grid_out_5, cell_grid_1_grid_out_4, cell_grid_1_grid_out_3, cell_grid_1_grid_out_2, cell_grid_1_grid_out}),
    .RST(RESET), .RUN_MODE(decoder_1_out2), .LOAD_MODE(decoder_1_out1), .CLK(and_1_out), .DATA_IN(DATA_IN),
    .DATA(fully_combined_memory_1_data), .SERIAL_OUT(DATA_OUT),
    .PARALEL_OUT(fully_combined_memory_1_paralel_out));
  DotMatrix #(.inputtype("row"), .matrixcols(8), .matrixrows(8)) CURRENT_STAGE (
    .row0(fully_combined_memory_1_data[7:0]), .row1(fully_combined_memory_1_data[15:8]),
    .row2(fully_combined_memory_1_data[23:16]), .row3(fully_combined_memory_1_data[31:24]),
    .row4(fully_combined_memory_1_data[39:32]), .row5(fully_combined_memory_1_data[47:40]),
    .row6(fully_combined_memory_1_data[55:48]), .row7(fully_combined_memory_1_data[63:56]));
  cell_grid cell_grid_1 (
    .GRID_IN(fully_combined_memory_1_data),
    .GRID_OUT({cell_grid_1_grid_out_8, cell_grid_1_grid_out_7, cell_grid_1_grid_out_6, cell_grid_1_grid_out_5, cell_grid_1_grid_out_4, cell_grid_1_grid_out_3, cell_grid_1_grid_out_2, cell_grid_1_grid_out}));
  // Probe on {cell_grid_1_grid_out_8, cell_grid_1_grid_out_7, cell_grid_1_grid_out_6, cell_grid_1_grid_out_5, cell_grid_1_grid_out_4, cell_grid_1_grid_out_3, cell_grid_1_grid_out_2, cell_grid_1_grid_out}
  DotMatrix #(.inputtype("row"), .matrixcols(8), .matrixrows(8)) NEXT_STAGE (
    .row0(cell_grid_1_grid_out), .row1(cell_grid_1_grid_out_2), .row2(cell_grid_1_grid_out_3),
    .row3(cell_grid_1_grid_out_4), .row4(cell_grid_1_grid_out_5), .row5(cell_grid_1_grid_out_6),
    .row6(cell_grid_1_grid_out_7), .row7(cell_grid_1_grid_out_8));
  // Probe on fully_combined_memory_1_paralel_out
  DotMatrix #(.inputtype("row"), .matrixcols(8), .matrixrows(8)) dotmatrix_1 (
    .row0(fully_combined_memory_1_paralel_out[7:0]), .row1(fully_combined_memory_1_paralel_out[15:8]),
    .row2(fully_combined_memory_1_paralel_out[23:16]), .row3(fully_combined_memory_1_paralel_out[31:24]),
    .row4(fully_combined_memory_1_paralel_out[39:32]), .row5(fully_combined_memory_1_paralel_out[47:40]),
    .row6(fully_combined_memory_1_paralel_out[55:48]), .row7(fully_combined_memory_1_paralel_out[63:56]));

  // Notes on the sheet:
  //   1. Set "MODE" to "01" (i.e. data in) and run clock 64 times to shift in all data
  //   2. Set mode to "10" (i.e. run) and clock to run the system
  //   3. To read out, set mode to "11" (i.e. data out), then clock 64 times to read out data
  //   4. Set RESET to high to async reset everything
  //   5. Set mode to "00" to disable clocking
  //   These are only accurate when in run mode
  //   This needs to stay separate, or shifting out would mess up the stored data
  //   Which would require us to clock back in after each clock out
  //   FIXME: How do I shift out backwards like how VHDL implementation does
  //   This is not accurate once we start clocking data out
endmodule

module looparound_memory (
  input  LOAD_MODE,
  input  OUTPUT_MODE,
  input  RST,
  input  RUN_MODE,
  input  DATA_IN,
  input  CLK,
  input  [63:0] GRID_IN,
  output [63:0] DATA,
  output SERIAL_OUT
);

  wire multiplexer_1_out, or_1_out;

  Multiplexer multiplexer_1 (.in0(DATA_IN), .in1(DATA[0]), .out(multiplexer_1_out), .sel(OUTPUT_MODE));
  or or_1 (or_1_out, LOAD_MODE, OUTPUT_MODE);
  // Shift_Register #(.length(64)) shift_register_1: pin names not known; wires that end beside it: RST, RUN_MODE, or_1_out, CLK, multiplexer_1_out, GRID_IN[63], GRID_IN[62], GRID_IN[61], GRID_IN[60], GRID_IN[59], GRID_IN[58], GRID_IN[57], GRID_IN[56], GRID_IN[55], GRID_IN[54], GRID_IN[53], GRID_IN[52], DATA[63], DATA[62], DATA[61], DATA[60], DATA[59], DATA[58], DATA[57], DATA[56], DATA[55], DATA[54], DATA[53], DATA[52]
  // Probe on DATA

  assign SERIAL_OUT = DATA[0];

  // Notes on the sheet:
  //   Like "fully_combined_memory" but instead of using two shift registers, 
  //   we only use 1, but when shifting out, we also loop the data around back into
  //   the system.
  //   Downside is that it means we can't do partial reads. You must always read exactly the size of the system
endmodule

module main_shift_based_v4 (
  input  DATA_IN,
  input  [1:0] MODE,
  input  RESET,
  output DATA_OUT
);

  wire and_1_out, CLK_out, decoder_1_out0, decoder_1_out1, decoder_1_out2, decoder_1_out3, not_1_out;
  wire [7:0] cell_grid_1_grid_out, cell_grid_1_grid_out_2, cell_grid_1_grid_out_3, cell_grid_1_grid_out_4,
       cell_grid_1_grid_out_5, cell_grid_1_grid_out_6, cell_grid_1_grid_out_7, cell_grid_1_grid_out_8;
  wire [63:0] looparound_memory_1_data;

  Decoder #(.select(2)) decoder_1 (
    .out0(decoder_1_out0), .out1(decoder_1_out1), .out2(decoder_1_out2), .out3(decoder_1_out3), .sel(MODE));  // open: en
  Clock CLK (.out(CLK_out));
  not not_1 (not_1_out, decoder_1_out0);
  and and_1 (and_1_out, not_1_out, CLK_out);
  // Probe on looparound_memory_1_data
  looparound_memory looparound_memory_1 (
    .DATA_IN(DATA_IN), .OUTPUT_MODE(decoder_1_out3), .LOAD_MODE(decoder_1_out1),
    .GRID_IN({cell_grid_1_grid_out_8, cell_grid_1_grid_out_7, cell_grid_1_grid_out_6, cell_grid_1_grid_out_5, cell_grid_1_grid_out_4, cell_grid_1_grid_out_3, cell_grid_1_grid_out_2, cell_grid_1_grid_out}),
    .RST(RESET), .RUN_MODE(decoder_1_out2), .CLK(and_1_out), .SERIAL_OUT(DATA_OUT),
    .DATA(looparound_memory_1_data));
  DotMatrix #(.inputtype("row"), .matrixcols(8), .matrixrows(8)) CURRENT_STAGE (
    .row0(looparound_memory_1_data[7:0]), .row1(looparound_memory_1_data[15:8]),
    .row2(looparound_memory_1_data[23:16]), .row3(looparound_memory_1_data[31:24]),
    .row4(looparound_memory_1_data[39:32]), .row5(looparound_memory_1_data[47:40]),
    .row6(looparound_memory_1_data[55:48]), .row7(looparound_memory_1_data[63:56]));
  // Probe on {cell_grid_1_grid_out_8, cell_grid_1_grid_out_7, cell_grid_1_grid_out_6, cell_grid_1_grid_out_5, cell_grid_1_grid_out_4, cell_grid_1_grid_out_3, cell_grid_1_grid_out_2, cell_grid_1_grid_out}
  DotMatrix #(.inputtype("row"), .matrixcols(8), .matrixrows(8)) NEXT_STAGE (
    .row0(cell_grid_1_grid_out), .row1(cell_grid_1_grid_out_2), .row2(cell_grid_1_grid_out_3),
    .row3(cell_grid_1_grid_out_4), .row4(cell_grid_1_grid_out_5), .row5(cell_grid_1_grid_out_6),
    .row6(cell_grid_1_grid_out_7), .row7(cell_grid_1_grid_out_8));
  cell_grid cell_grid_1 (
    .GRID_IN(looparound_memory_1_data),
    .GRID_OUT({cell_grid_1_grid_out_8, cell_grid_1_grid_out_7, cell_grid_1_grid_out_6, cell_grid_1_grid_out_5, cell_grid_1_grid_out_4, cell_grid_1_grid_out_3, cell_grid_1_grid_out_2, cell_grid_1_grid_out}));

  // Notes on the sheet:
  //   1. Set "MODE" to "01" (i.e. data in) and run clock 64 times to shift in all data
  //   2. Set mode to "10" (i.e. run) and clock to run the system
  //   3. To read out, set mode to "11" (i.e. data out), then clock 64 times to read out data
  //   4. Set RESET to high to async reset everything
  //   5. Set mode to "00" to disable clocking
  //   These are only accurate when in run mode
  //   Which would require us to clock back in after each clock out
  //   This needs to stay separate, or shifting out would mess up the stored data
  //   FIXME: How do I shift out backwards like how VHDL implementation does
endmodule

module single_row_calc (
  input  [7:0] PREV_ROW,
  input  [7:0] THIS_ROW,
  input  [7:0] NEXT_ROW,
  output [7:0] ROW_ALIVE
);

  wire CELL_0_0_me_e, CELL_0_1_me_e, CELL_0_1_me_w, CELL_0_2_me_e, CELL_0_2_me_w, CELL_0_3_me_e,
       CELL_0_3_me_w, CELL_0_4_me_e, CELL_0_4_me_w, CELL_0_5_me_e, CELL_0_5_me_w, CELL_0_6_me_e,
       CELL_0_6_me_w, CELL_0_7_me_w;

  single_cell CELL_0_0 (
    .NE(PREV_ROW[1]), .N(PREV_ROW[0]), .NW(1'b0), .W(1'b0), .E(CELL_0_1_me_w), .SW(1'b0), .S(NEXT_ROW[0]),
    .SE(NEXT_ROW[1]), .ME(THIS_ROW[0]), .ALIVE(ROW_ALIVE[0]), .ME_E(CELL_0_0_me_e));  // open: ME_N, ME_S, ME_W
  single_cell CELL_0_1 (
    .NE(PREV_ROW[2]), .N(PREV_ROW[1]), .NW(PREV_ROW[0]), .W(CELL_0_0_me_e), .E(CELL_0_2_me_w),
    .SW(NEXT_ROW[0]), .S(NEXT_ROW[1]), .SE(NEXT_ROW[2]), .ME(THIS_ROW[1]), .ALIVE(ROW_ALIVE[1]),
    .ME_E(CELL_0_1_me_e), .ME_W(CELL_0_1_me_w));  // open: ME_N, ME_S
  single_cell CELL_0_2 (
    .NE(PREV_ROW[3]), .N(PREV_ROW[2]), .NW(PREV_ROW[1]), .W(CELL_0_1_me_e), .E(CELL_0_3_me_w),
    .SW(NEXT_ROW[1]), .S(NEXT_ROW[2]), .SE(NEXT_ROW[3]), .ME(THIS_ROW[2]), .ALIVE(ROW_ALIVE[2]),
    .ME_E(CELL_0_2_me_e), .ME_W(CELL_0_2_me_w));  // open: ME_N, ME_S
  single_cell CELL_0_3 (
    .NE(PREV_ROW[4]), .N(PREV_ROW[3]), .NW(PREV_ROW[2]), .W(CELL_0_2_me_e), .E(CELL_0_4_me_w),
    .SW(NEXT_ROW[2]), .S(NEXT_ROW[3]), .SE(NEXT_ROW[4]), .ME(THIS_ROW[3]), .ALIVE(ROW_ALIVE[3]),
    .ME_E(CELL_0_3_me_e), .ME_W(CELL_0_3_me_w));  // open: ME_N, ME_S
  single_cell CELL_0_4 (
    .NE(PREV_ROW[5]), .N(PREV_ROW[4]), .NW(PREV_ROW[3]), .W(CELL_0_3_me_e), .E(CELL_0_5_me_w),
    .SW(NEXT_ROW[3]), .S(NEXT_ROW[4]), .SE(NEXT_ROW[5]), .ME(THIS_ROW[4]), .ALIVE(ROW_ALIVE[4]),
    .ME_E(CELL_0_4_me_e), .ME_W(CELL_0_4_me_w));  // open: ME_N, ME_S
  single_cell CELL_0_5 (
    .NE(PREV_ROW[6]), .N(PREV_ROW[5]), .NW(PREV_ROW[4]), .W(CELL_0_4_me_e), .E(CELL_0_6_me_w),
    .SW(NEXT_ROW[4]), .S(NEXT_ROW[5]), .SE(NEXT_ROW[6]), .ME(THIS_ROW[5]), .ALIVE(ROW_ALIVE[5]),
    .ME_E(CELL_0_5_me_e), .ME_W(CELL_0_5_me_w));  // open: ME_N, ME_S
  single_cell CELL_0_6 (
    .NE(PREV_ROW[7]), .N(PREV_ROW[6]), .NW(PREV_ROW[5]), .W(CELL_0_5_me_e), .E(CELL_0_7_me_w),
    .SW(NEXT_ROW[5]), .S(NEXT_ROW[6]), .SE(NEXT_ROW[7]), .ME(THIS_ROW[6]), .ALIVE(ROW_ALIVE[6]),
    .ME_E(CELL_0_6_me_e), .ME_W(CELL_0_6_me_w));  // open: ME_N, ME_S
  single_cell CELL_0_7 (
    .NE(1'b0), .N(PREV_ROW[7]), .NW(PREV_ROW[6]), .W(CELL_0_6_me_e), .E(1'b0), .SW(NEXT_ROW[6]),
    .S(NEXT_ROW[7]), .SE(1'b0), .ME(THIS_ROW[7]), .ALIVE(ROW_ALIVE[7]), .ME_W(CELL_0_7_me_w));  // open: ME_N, ME_S, ME_E
endmodule

module shifter_inc8 (
  input  SERIAL_IN,
  input  [7:0] IN_HIGH_8,
  input  SERIAL_IN_EN,
  input  CIRCULAR_SHIFT_UP_EN,
  input  LOAD_8_SHIFT_DOWN_EN,
  input  CLK,
  input  RESET,
  output [63:0] OUT_PARALLEL,
  output OUT_SERIAL
);

  wire or_1_out;
  wire [1:0] priority_encoder_1_out;
  wire [63:0] multiplexer_1_out, set_high_8_1_result, set_low_bit_1_result, shifter_1_out, shifter_2_out;

  or or_1 (or_1_out, SERIAL_IN_EN, CIRCULAR_SHIFT_UP_EN, LOAD_8_SHIFT_DOWN_EN);
  set_low_bit set_low_bit_1 (.DATA(shifter_1_out), .NEW_BIT(SERIAL_IN), .RESULT(set_low_bit_1_result));
  set_high_8 set_high_8_1 (.DATA(shifter_2_out), .NEW_BITS(IN_HIGH_8), .RESULT(set_high_8_1_result));
  Priority_Encoder #(.select(2)) priority_encoder_1 (
    .in0(1'b1), .in1(SERIAL_IN_EN), .in2(CIRCULAR_SHIFT_UP_EN), .in3(LOAD_8_SHIFT_DOWN_EN),
    .out(priority_encoder_1_out));  // open: gs, en_out, en_in
  Multiplexer #(.select(2), .width(64)) multiplexer_1 (
    .in0(OUT_PARALLEL), .in1(set_low_bit_1_result), .in2(shifter_1_out), .in3(set_high_8_1_result),
    .out(multiplexer_1_out), .sel(priority_encoder_1_out));
  Register #(.width(64)) register_1 (.D(multiplexer_1_out), .en(or_1_out), .clk(CLK), .Q(OUT_PARALLEL), .clr(RESET));
  Shifter #(.shift("rl"), .width(64)) shifter_1 (.in(OUT_PARALLEL), .\dist (6'b000001), .out(shifter_1_out));
  DotMatrix #(.inputtype("row"), .matrixcols(8), .matrixrows(8)) dotmatrix_1 (
    .row0(OUT_PARALLEL[7:0]), .row1(OUT_PARALLEL[15:8]), .row2(OUT_PARALLEL[23:16]),
    .row3(OUT_PARALLEL[31:24]), .row4(OUT_PARALLEL[39:32]), .row5(OUT_PARALLEL[47:40]),
    .row6(OUT_PARALLEL[55:48]), .row7(OUT_PARALLEL[63:56]));
  Shifter #(.shift("lr"), .width(64)) shifter_2 (.in(OUT_PARALLEL), .\dist (6'b001000), .out(shifter_2_out));

  assign OUT_SERIAL = OUT_PARALLEL[63];

  // Notes on the sheet:
  //   Shifts up by 1
  //   Shifts down by 8
endmodule

module system_counter (
  input  ENABLE,
  input  RESET,
  input  CLK,
  output IS_MAX
);

  wire or_1_out;
  wire [3:0] counter_1_q;

  or or_1 (or_1_out, ~ENABLE, RESET);  // OR_Gate
  Counter #(.max('h7), .width(4)) counter_1 (
    .clr(or_1_out), .count(ENABLE), .clk(CLK), .Q(counter_1_q));  // open: load, up, D, carry
  Comparator #(.width(4)) comparator_1 (.a(counter_1_q), .b(4'b0111), .eq(IS_MAX));  // open: gt, lt
endmodule

module system_memory_by_row (
  input  LOAD_MODE,
  input  RUN_MODE,
  input  OUTPUT_MODE,
  input  RESET,
  input  CLK,
  input  SERIAL_IN,
  input  [7:0] TOP_8_IN,
  output [7:0] PREV_ROW,
  output [63:0] PARALLEL_OUT,
  output [7:0] CURRENT_ROW,
  output [7:0] NEXT_ROW,
  output SERIAL_OUT
);

  wire and_1_out;

  shifter_inc8 shifter_inc8_1 (
    .SERIAL_IN(SERIAL_IN), .IN_HIGH_8(TOP_8_IN), .SERIAL_IN_EN(LOAD_MODE),
    .CIRCULAR_SHIFT_UP_EN(OUTPUT_MODE), .LOAD_8_SHIFT_DOWN_EN(RUN_MODE), .CLK(CLK), .RESET(RESET),
    .OUT_PARALLEL({PARALLEL_OUT[63:16], NEXT_ROW, CURRENT_ROW}), .OUT_SERIAL(SERIAL_OUT));
  and and_1 (and_1_out, LOAD_MODE, RESET);
  Register PREV_ROW_MEM (.D(CURRENT_ROW), .en(RUN_MODE), .clk(CLK), .Q(PREV_ROW), .clr(and_1_out));

  assign PARALLEL_OUT[15:0] = {NEXT_ROW, CURRENT_ROW};
endmodule

module grid_calc_row_by_row (
  input  SERIAL_IN,
  input  LOAD_MODE,
  input  RUN_MODE,
  input  OUTPUT_MODE,
  input  RESET,
  output SERIAL_OUT
);

  wire clock_1_out, system_counter_1_is_max;
  wire [7:0] multiplexer_1_out, single_row_calc_1_row_alive, system_memory_by_row_1_current_row,
       system_memory_by_row_1_next_row, system_memory_by_row_1_prev_row;
  wire [63:0] system_memory_by_row_1_parallel_out;

  Clock clock_1 (.out(clock_1_out));
  system_counter system_counter_1 (
    .ENABLE(RUN_MODE), .RESET(RESET), .CLK(clock_1_out), .IS_MAX(system_counter_1_is_max));
  system_memory_by_row system_memory_by_row_1 (
    .CLK(clock_1_out), .SERIAL_IN(SERIAL_IN), .LOAD_MODE(LOAD_MODE), .RUN_MODE(RUN_MODE),
    .OUTPUT_MODE(OUTPUT_MODE), .RESET(RESET), .TOP_8_IN(single_row_calc_1_row_alive),
    .PARALLEL_OUT(system_memory_by_row_1_parallel_out), .CURRENT_ROW(system_memory_by_row_1_current_row),
    .NEXT_ROW(system_memory_by_row_1_next_row), .SERIAL_OUT(SERIAL_OUT),
    .PREV_ROW(system_memory_by_row_1_prev_row));
  DotMatrix #(.inputtype("row"), .matrixcols(8), .matrixrows(8)) MEMORY_DATA (
    .row0(system_memory_by_row_1_parallel_out[7:0]), .row1(system_memory_by_row_1_parallel_out[15:8]),
    .row2(system_memory_by_row_1_parallel_out[23:16]), .row3(system_memory_by_row_1_parallel_out[31:24]),
    .row4(system_memory_by_row_1_parallel_out[39:32]), .row5(system_memory_by_row_1_parallel_out[47:40]),
    .row6(system_memory_by_row_1_parallel_out[55:48]), .row7(system_memory_by_row_1_parallel_out[63:56]));
  Multiplexer #(.width(8)) multiplexer_1 (
    .in0(system_memory_by_row_1_next_row), .in1({8{1'b0}}), .out(multiplexer_1_out),
    .sel(system_counter_1_is_max));
  DotMatrix #(.inputtype("row"), .matrixcols(8), .matrixrows(1)) PREV_ROW (.row0(system_memory_by_row_1_prev_row));
  single_row_calc single_row_calc_1 (
    .PREV_ROW(system_memory_by_row_1_prev_row), .THIS_ROW(system_memory_by_row_1_current_row),
    .NEXT_ROW(multiplexer_1_out), .ROW_ALIVE(single_row_calc_1_row_alive));
endmodule

module set_low_bit (
  input  [63:0] DATA,
  input  NEW_BIT,
  output [63:0] RESULT
);


  assign RESULT = {DATA[63:1], NEW_BIT};

  // Notes on the sheet:
  //   Sets the lowest bit to the given value
endmodule

module set_high_8 (
  input  [63:0] DATA,
  input  [7:0] NEW_BITS,
  output [63:0] RESULT
);


  assign RESULT = {NEW_BITS, DATA[55:0]};
endmodule

module vgatest (
  input  RESET,
  input  [6:0] x,
  input  [6:0] y
);

  wire clock_1_out;

  Clock clock_1 (.out(clock_1_out));
  // RGB_Video rgb_video_1: pin names not known; wires that end beside it: RESET, clock_1_out, x, y
endmodule
